# Fritzing sketch sEMG_circuits (saved by Fritzing 0.9.5d)
breadboards: 1

parts:
  M1 = advancer muscle sensor v3
  A1 = Arduino UNO R4 WiFi
  M2 = advancer muscle sensor v3
  M3 = advancer muscle sensor v3
  M4 = advancer muscle sensor v3
  VCC1 = Battery block 9V
  VCC2 = Battery block 9V

nets:
  N1: M1.+Vs, M2.+Vs, M3.+Vs, M4.+Vs, VCC1.+
  GND: M1.GND, A1.Pin_10, A1.Pin_25, A1.Pin_48, M2.GND, M3.GND, M4.GND, VCC1.-, VCC2.+
  N2: M1.-Vs, M2.-Vs, M3.-Vs, M4.-Vs, VCC2.-
  N3: M1.SIG, A1.Pin_15
  N4: A1.Pin_12, M4.SIG
  N5: A1.Pin_13, M3.SIG
  N6: A1.Pin_14, M2.SIG

custom parts:
  advancer muscle sensor v3: This sensor will measure the filtered and rectified electrical activity of a muscle; outputting 0-Vs Volts depending the amount of activity in the selected muscle, where Vs signifies the voltage of the power source. Power supply voltage: min. +-3.5V.
  Arduino UNO R4 WiFi: The Arduino UNO R4 WiFi merges the RA4M1 microprocessor from Renesas with the ESP32-S3 from Espressif, creating an all-in-one tool for makers with enhanced processing power and a diverse array of new peripherals.
